// Digital circuit alu.dig as structural Verilog
module alu (
  input  SelectA,
  input  SelectB,
  input  [7:0] LHSIn,
  input  CarryIn,
  input  [7:0] RHSIn,
  input  ClockIn,
  output CarryOut,
  output [7:0] AdderOut
);

  wire shift_1_carryout;
  wire [7:0] shift_1_lhsout;

  shift shift_1 (
    .SelectA(SelectA), .SelectB(SelectB), .LHSIn(LHSIn), .CarryIn(CarryIn), .CarryOut(shift_1_carryout),
    .LHSOut(shift_1_lhsout));
  adder adder_1 (
    .ClockIn(ClockIn), .LHS(shift_1_lhsout), .RHS(RHSIn), .CarryIn(shift_1_carryout), .CarryOut(CarryOut),
    .AdderOut(AdderOut));
endmodule
