// Digital circuit memory.dig as structural Verilog
module memory (
  input  MemBridge__Direction,
  input  MemBridge__Load,
  input  [15:0] Addr,
  input  [7:0] MEMDATAIn,
  output [7:0] MEMDATAOut
);

  wire not_1_out, not_2_out, not_4_out, nOutputEnable, nRamCE, nRamWE, nRomCE;

  not not_1 (not_1_out, MemBridge__Load);
  not not_2 (not_2_out, not_1_out);
  not not_3 (nOutputEnable, MemBridge__Direction);
  not not_4 (not_4_out, not_2_out);
  _74138 _74138_1 (
    .pin1(Addr[15]), .pin2(1'b0), .pin3(1'b0), .pin4(1'b0), .pin5(1'b0), .pin6(1'b1), .pin8(1'b0),
    .pin14(nRamCE), .pin15(nRomCE), .pin16(1'b1));  // open: pin7, pin9, pin10, pin11, pin12, pin13
  not not_5 (nRamWE, not_4_out);
  // _28c256 _28c256_1: pin names not known; wires that end beside it: Addr[14], Addr[12], Addr[7], Addr[6], Addr[5], Addr[4], Addr[3], Addr[2], Addr[1], Addr[0], MEMDATAIn[0], MEMDATAIn[1], MEMDATAIn[2], 1'b0, 1'b1, 1'b1, Addr[13], Addr[8], Addr[9], Addr[0], nOutputEnable, Addr[10], nRomCE, MEMDATAIn[7]
  _62256 _62256_1 (
    .nCE(nRamCE), .nOE(nOutputEnable), .nWE(nRamWE), .VCC(1'b1), .GND(1'b0), .I_O0(MEMDATAIn[0]),
    .I_O1(MEMDATAIn[1]), .I_O2(MEMDATAIn[2]), .I_O3(MEMDATAIn[3]), .I_O4(MEMDATAIn[4]), .I_O5(MEMDATAIn[5]),
    .I_O6(MEMDATAIn[6]), .I_O7(MEMDATAIn[7]), .A0(Addr[0]), .A1(Addr[1]), .A2(Addr[2]), .A3(Addr[3]),
    .A4(Addr[4]), .A5(Addr[5]), .A6(Addr[6]), .A7(Addr[7]), .A8(Addr[8]), .A9(Addr[9]), .A10(Addr[10]),
    .A11(Addr[0]), .A12(Addr[12]), .A13(Addr[13]), .A14(Addr[14]));

  assign MEMDATAOut = MEMDATAIn;

  // Other names for the same wires on the sheet: MEMDATA[7:0] = MEMDATAIn; MEMDATA0 = MEMDATAIn[0];
  //   MEMDATA1 = MEMDATAIn[1]; MEMDATA2 = MEMDATAIn[2]; MEMDATA3 = MEMDATAIn[3]; MEMDATA4 = MEMDATAIn[4];
  //   MEMDATA5 = MEMDATAIn[5]; MEMDATA6 = MEMDATAIn[6]; MEMDATA7 = MEMDATAIn[7]
endmodule

/* Test case Simple Tests:
MemBridge\_Load MemBridge\_Direction 	Addr 	MEMDATAIn 	MEMDATAOut
# read from ROM
1		1			0x0000	z		x
1		1			0x0000	z		0

# write to RAM
1		0			0x8000	0xFF		x
0		0			0x8000	0xFF		x

# verify write
1		1			0x8000	z		x
1		1			0x8000	z		0xFF
*/
